// Digital circuit SOP.dig as structural Verilog
module SOP (
  input  X,
  input  Y,
  input  Z,
  output out_4
);

  wire not_1_out, not_2_out, or_1_out;

  not not_1 (not_1_out, X);
  not not_2 (not_2_out, Y);
  or or_1 (or_1_out, not_1_out, not_2_out);
  and and_1 (out_4, or_1_out, Z);
endmodule
