// Digital circuit Full_Adder.dig as structural Verilog
module Full_Adder (
  input  A,
  input  B,
  input  C,
  output X__Carry,
  output Y__Sum
);

  wire and_1_out, and_2_out, xor_1_out;

  xor xor_1 (xor_1_out, A, B);
  xor xor_2 (Y__Sum, xor_1_out, C);
  and and_1 (and_1_out, xor_1_out, C);
  and and_2 (and_2_out, A, B);
  or or_1 (X__Carry, and_1_out, and_2_out);
endmodule
