// Digital circuit Half_Adder.dig as structural Verilog
module Half_Adder (
  input  A,
  input  B,
  output Y__Sum,
  output X__Carry
);

  xor xor_1 (Y__Sum, A, B);
  and and_1 (X__Carry, A, B);
endmodule
