// Digital circuit Adder Subtractor 1.dig as structural Verilog
module Adder_Subtractor_1 (
  input  A,
  input  B,
  input  C,
  input  D,
  input  E,
  input  F,
  input  G,
  input  H,
  input  in_14,
  output Y,
  output X,
  output Z,
  output U,
  output V
);

  wire add_2_c_o, add_3_c_o, add_4_c_o, and_1_out, multiplexer_1_out, multiplexer_2_out, multiplexer_3_out,
       multiplexer_4_out, not_1_out, not_2_out, not_3_out, not_4_out, not_5_out;

  LED led_1 (.in(and_1_out));
  not not_1 (not_1_out, V);
  and and_1 (and_1_out, in_14, not_1_out);
  Add add_1 (.a(multiplexer_1_out), .b(E), .c_i(add_2_c_o), .s(Y), .c_o(V));
  Add add_2 (.a(multiplexer_2_out), .b(F), .c_i(add_3_c_o), .s(X), .c_o(add_2_c_o));
  Add add_3 (.a(multiplexer_3_out), .b(G), .c_i(add_4_c_o), .s(Z), .c_o(add_3_c_o));
  Add add_4 (.a(multiplexer_4_out), .b(H), .c_i(in_14), .s(U), .c_o(add_4_c_o));
  Multiplexer multiplexer_1 (.sel(in_14), .in_0(A), .in_1(not_2_out), .out(multiplexer_1_out));
  not not_2 (not_2_out, A);
  Multiplexer multiplexer_2 (.sel(in_14), .in_0(B), .in_1(not_3_out), .out(multiplexer_2_out));
  not not_3 (not_3_out, B);
  Multiplexer multiplexer_3 (.sel(in_14), .in_0(C), .in_1(not_4_out), .out(multiplexer_3_out));
  not not_4 (not_4_out, C);
  Multiplexer multiplexer_4 (.sel(in_14), .in_0(D), .in_1(not_5_out), .out(multiplexer_4_out));
  not not_5 (not_5_out, D);
endmodule
