// Digital circuit Ripple Carry Adder 2-bit.dig as structural Verilog
module Ripple_Carry_Adder_2_bit (
  input  A,
  input  B,
  input  C,
  input  D,
  output Y,
  output X,
  output Z
);

  wire add_2_c_o;

  Add add_1 (.a(A), .b(C), .c_i(add_2_c_o), .s(X), .c_o(Z));
  Add add_2 (.a(B), .b(D), .c_i(1'b0), .s(Y), .c_o(add_2_c_o));
endmodule
