// Digital circuit Ripple Carry Adder 4-bit.dig as structural Verilog
module Ripple_Carry_Adder_4_bit (
  input  A,
  input  B,
  input  C,
  input  D,
  input  E,
  input  F,
  input  G,
  input  H,
  output Y,
  output X,
  output Z,
  output U,
  output V
);

  wire add_2_c_o, add_3_c_o, add_4_c_o;

  Add add_1 (.a(A), .b(E), .c_i(add_2_c_o), .s(Y), .c_o(V));
  Add add_2 (.a(B), .b(F), .c_i(add_3_c_o), .s(X), .c_o(add_2_c_o));
  Add add_3 (.a(C), .b(G), .c_i(add_4_c_o), .s(Z), .c_o(add_3_c_o));
  Add add_4 (.a(D), .b(H), .c_i(1'b0), .s(U), .c_o(add_4_c_o));
endmodule
