// Digital circuit 8 Bit Adder Subtractor.dig as structural Verilog
module _8_Bit_Adder_Subtractor (
  input  B3,
  input  B2,
  input  B1,
  input  B0,
  input  A_S,
  input  A7,
  input  A6,
  input  A5,
  input  A4,
  input  A3,
  input  A2,
  input  A1,
  input  A0,
  input  B7,
  input  B6,
  input  B5,
  input  B4,
  output Overflow,
  output Y0,
  output Y1,
  output Y2,
  output Y3,
  output Y4,
  output Y5,
  output Y6,
  output Y7
);

  wire and_1_out, and_2_out, FA1_c_o, FA2_c_o, FA3_c_o, FA4_c_o, FA5_c_o, FA6_c_o, FA7_c_o,
       multiplexer_1_out, multiplexer_2_out, multiplexer_3_out, multiplexer_4_out, multiplexer_5_out,
       multiplexer_6_out, multiplexer_7_out, multiplexer_8_out, not_1_out, not_2_out, not_3_out, not_4_out,
       not_5_out, not_6_out, not_7_out, not_8_out, not_9_out, not_10_out, not_11_out;

  or or_1 (Overflow, and_2_out, and_1_out);
  and and_1 (and_1_out, not_1_out, B7, multiplexer_1_out);
  and and_2 (and_2_out, Y7, not_2_out, not_3_out);
  not not_1 (not_1_out, Y7);
  Add FA8 (.a(multiplexer_1_out), .b(B7), .c_i(FA7_c_o), .s(Y7));  // open: c_o
  not not_2 (not_2_out, B7);
  Add FA7 (.a(multiplexer_2_out), .b(B6), .c_i(FA6_c_o), .s(Y6), .c_o(FA7_c_o));
  not not_3 (not_3_out, multiplexer_1_out);
  Add FA6 (.a(multiplexer_3_out), .b(B5), .c_i(FA5_c_o), .s(Y5), .c_o(FA6_c_o));
  Add FA5 (.a(multiplexer_4_out), .b(B4), .c_i(FA4_c_o), .s(Y4), .c_o(FA5_c_o));
  Add FA4 (.a(multiplexer_5_out), .b(B3), .c_i(FA3_c_o), .s(Y3), .c_o(FA4_c_o));
  Add FA3 (.a(multiplexer_6_out), .b(B2), .c_i(FA2_c_o), .s(Y2), .c_o(FA3_c_o));
  Add FA2 (.a(multiplexer_7_out), .b(B1), .c_i(FA1_c_o), .s(Y1), .c_o(FA2_c_o));
  Add FA1 (.a(multiplexer_8_out), .b(B0), .c_i(A_S), .s(Y0), .c_o(FA1_c_o));
  Multiplexer multiplexer_1 (.sel(A_S), .in_0(A7), .in_1(not_4_out), .out(multiplexer_1_out));
  Multiplexer multiplexer_2 (.sel(A_S), .in_0(A6), .in_1(not_5_out), .out(multiplexer_2_out));
  not not_4 (not_4_out, A7);
  Multiplexer multiplexer_3 (.sel(A_S), .in_0(A5), .in_1(not_6_out), .out(multiplexer_3_out));
  not not_5 (not_5_out, A6);
  Multiplexer multiplexer_4 (.sel(A_S), .in_0(A4), .in_1(not_7_out), .out(multiplexer_4_out));
  not not_6 (not_6_out, A5);
  Multiplexer multiplexer_5 (.sel(A_S), .in_0(A3), .in_1(not_8_out), .out(multiplexer_5_out));
  not not_7 (not_7_out, A4);
  Multiplexer multiplexer_6 (.sel(A_S), .in_0(A2), .in_1(not_9_out), .out(multiplexer_6_out));
  not not_8 (not_8_out, A3);
  Multiplexer multiplexer_7 (.sel(A_S), .in_0(A1), .in_1(not_10_out), .out(multiplexer_7_out));
  not not_9 (not_9_out, A2);
  Multiplexer multiplexer_8 (.sel(A_S), .in_0(A0), .in_1(not_11_out), .out(multiplexer_8_out));
  not not_10 (not_10_out, A1);
  not not_11 (not_11_out, A0);
endmodule
