// Digital circuit Adder Subtractor 1.dig as structural Verilog
module Adder_Subtractor_1 (
  input  A3,
  input  A2,
  input  A1,
  input  A0,
  input  B3,
  input  B2,
  input  B1,
  input  B0,
  input  A_S,
  output Y4,
  output Y3,
  output Y1,
  output Y0,
  output Overflow
);

  wire and_1_out, and_2_out, Full_Adder_1_c_o, Full_Adder_2_c_o, Full_Adder_3_c_o, multiplexer_1_out,
       multiplexer_2_out, multiplexer_3_out, multiplexer_4_out, not_1_out, not_2_out, not_3_out, not_4_out,
       not_5_out, not_6_out, not_7_out;

  or or_1 (Overflow, and_2_out, and_1_out);
  and and_1 (and_1_out, not_1_out, B3, multiplexer_1_out);
  and and_2 (and_2_out, Y4, not_2_out, not_3_out);
  not not_1 (not_1_out, Y4);
  not not_2 (not_2_out, B3);
  not not_3 (not_3_out, multiplexer_1_out);
  Add Full_Adder_4 (.a(multiplexer_1_out), .b(B3), .c_i(Full_Adder_3_c_o), .s(Y4));  // open: c_o
  Add Full_Adder_3 (.a(multiplexer_2_out), .b(B2), .c_i(Full_Adder_2_c_o), .s(Y3), .c_o(Full_Adder_3_c_o));
  Add Full_Adder_2 (.a(multiplexer_3_out), .b(B1), .c_i(Full_Adder_1_c_o), .s(Y1), .c_o(Full_Adder_2_c_o));
  Add Full_Adder_1 (.a(multiplexer_4_out), .b(B0), .c_i(A_S), .s(Y0), .c_o(Full_Adder_1_c_o));
  Multiplexer multiplexer_1 (.sel(A_S), .in_0(A3), .in_1(not_4_out), .out(multiplexer_1_out));
  not not_4 (not_4_out, A3);
  Multiplexer multiplexer_2 (.sel(A_S), .in_0(A2), .in_1(not_5_out), .out(multiplexer_2_out));
  not not_5 (not_5_out, A2);
  Multiplexer multiplexer_3 (.sel(A_S), .in_0(A1), .in_1(not_6_out), .out(multiplexer_3_out));
  not not_6 (not_6_out, A1);
  Multiplexer multiplexer_4 (.sel(A_S), .in_0(A0), .in_1(not_7_out), .out(multiplexer_4_out));
  not not_7 (not_7_out, A0);
endmodule
