// Digital circuit Flip_Bits.dig as structural Verilog
module Flip_Bits (
  input  A0,
  input  A1,
  input  A2,
  input  A3,
  input  C,
  output Y1,
  output Y2,
  output Y3,
  output Y4
);

  wire not_1_out, not_2_out, not_3_out, not_4_out;

  not not_1 (not_1_out, A3);
  Multiplexer multiplexer_1 (.sel(C), .in_0(A3), .in_1(not_1_out), .out(Y4));
  not not_2 (not_2_out, A2);
  Multiplexer multiplexer_2 (.sel(C), .in_0(A2), .in_1(not_2_out), .out(Y3));
  not not_3 (not_3_out, A1);
  Multiplexer multiplexer_3 (.sel(C), .in_0(A1), .in_1(not_3_out), .out(Y2));
  not not_4 (not_4_out, A0);
  Multiplexer multiplexer_4 (.sel(C), .in_0(A0), .in_1(not_4_out), .out(Y1));
endmodule
