// Digital circuit Full_Adder_Rep.dig as structural Verilog
module Full_Adder_Rep (
  input  A,
  input  B,
  input  Carry_In__C,
  output Sum__X,
  output Carry_Out__Y
);

  Add add_1 (.a(A), .b(B), .c_i(Carry_In__C), .s(Sum__X), .c_o(Carry_Out__Y));
endmodule
