// Digital circuit Multiplexor.dig as structural Verilog
module Multiplexor (
  input  A,
  input  B,
  input  C,
  output Y
);

  Multiplexer multiplexer_1 (.sel(C), .in_0(B), .in_1(A), .out(Y));
endmodule
