// Digital circuit Ripple Carry Adder 2-bit.dig as structural Verilog
module Ripple_Carry_Adder_2_bit (
  input  A1,
  input  A0,
  input  B1,
  input  B0,
  output Y0,
  output Y1,
  output Carry
);

  wire Full_Adder_1_c_o;

  Add Full_Adder_2 (.a(A1), .b(B1), .c_i(Full_Adder_1_c_o), .s(Y1), .c_o(Carry));
  Add Full_Adder_1 (.a(A0), .b(B0), .c_i(1'b0), .s(Y0), .c_o(Full_Adder_1_c_o));
endmodule
