// Digital circuit Ripple Carry Adder 4-bit.dig as structural Verilog
module Ripple_Carry_Adder_4_bit (
  input  A3,
  input  A2,
  input  A1,
  input  A0,
  input  B3,
  input  B2,
  input  B1,
  input  B0,
  output Y3,
  output Y2,
  output Y1,
  output Y0,
  output Carry
);

  wire Full_Adder_1_c_o, Full_Adder_2_c_o, Full_Adder_3_c_o;

  Add Full_Adder_4 (.a(A3), .b(B3), .c_i(Full_Adder_3_c_o), .s(Y3), .c_o(Carry));
  Add Full_Adder_3 (.a(A2), .b(B2), .c_i(Full_Adder_2_c_o), .s(Y2), .c_o(Full_Adder_3_c_o));
  Add Full_Adder_2 (.a(A1), .b(B1), .c_i(Full_Adder_1_c_o), .s(Y1), .c_o(Full_Adder_2_c_o));
  Add Full_Adder_1 (.a(A0), .b(B0), .c_i(1'b0), .s(Y0), .c_o(Full_Adder_1_c_o));
endmodule
