// Digital circuit 1-bit_ALU_1.dig as structural Verilog
module _1_bit_ALU_1 (
  input  B1,
  input  A_S,
  input  A1,
  output Y
);

  wire multiplexer_1_out, not_1_out;

  Add _1_Bit_Full_Adder (.a(multiplexer_1_out), .b(B1), .c_i(A_S), .s(Y));  // open: c_o
  not not_1 (not_1_out, A1);
  Multiplexer multiplexer_1 (.sel(A_S), .in_0(A1), .in_1(not_1_out), .out(multiplexer_1_out));
endmodule
