// Digital circuit 1-bit_ALU_2.dig as structural Verilog
module _1_bit_ALU_2 (
  input  B1,
  input  A_S,
  input  A1,
  output Y,
  output Y_2,
  output Carry,
  output Overflow
);

  wire multiplexer_1_out, not_1_out;

  xor xor_1 (Overflow, Carry, A_S);
  Add _1_Bit_Full_Adder (.a(multiplexer_1_out), .b(B1), .c_i(A_S), .s(Y), .c_o(Carry));
  not not_1 (not_1_out, A1);
  Multiplexer multiplexer_1 (.sel(A_S), .in_0(A1), .in_1(not_1_out), .out(multiplexer_1_out));
  and and_1 (Y_2, A1, B1);
endmodule
