// Digital circuit 1-bit_ALU_4.dig as structural Verilog
module _1_bit_ALU_4 (
  input  B1,
  input  Operand_1__A_S,
  input  A1,
  input  Operand_2,
  output Carry,
  output Overflow,
  output Y
);

  wire _1_Bit_Full_Adder_s, and_1_out, multiplexer_1_out, multiplexer_3_out, not_1_out, xor_2_out;

  xor xor_1 (Overflow, Carry, Operand_1__A_S);
  Add _1_Bit_Full_Adder (.a(multiplexer_1_out), .b(B1), .c_i(Operand_1__A_S), .s(_1_Bit_Full_Adder_s), .c_o(Carry));
  not not_1 (not_1_out, A1);
  Multiplexer multiplexer_1 (.sel(Operand_1__A_S), .in_0(A1), .in_1(not_1_out), .out(multiplexer_1_out));
  Multiplexer multiplexer_2 (.sel(Operand_2), .in_0(multiplexer_3_out), .in_1(_1_Bit_Full_Adder_s), .out(Y));
  and and_1 (and_1_out, A1, B1);
  Multiplexer multiplexer_3 (.sel(Operand_1__A_S), .in_0(xor_2_out), .in_1(and_1_out), .out(multiplexer_3_out));
  xor xor_2 (xor_2_out, A1, B1);
endmodule
