// Digital circuit 4-bit_ALU.dig as structural Verilog
module _4_bit_ALU (
  input  A0,
  input  A1,
  input  A2,
  input  A3,
  input  B3,
  input  B2,
  input  B1,
  input  B0,
  input  Operand_1,
  input  Operand_2,
  output Y0,
  output Y1,
  output Y2,
  output Y3
);

  wire _7483_1_pin2, _7483_1_pin3, _7483_1_pin6, _7483_1_pin8, _7483_1_pin9, _7483_1_pin10, _7483_1_pin15,
       and_1_out, and_2_out, and_3_out, and_4_out, multiplexer_1_out, multiplexer_9_out, multiplexer_10_out,
       multiplexer_11_out, multiplexer_12_out, not_1_out, not_2_out, not_3_out, not_4_out, xor_1_out,
       xor_2_out, xor_3_out, xor_4_out;

  not not_1 (not_1_out, A3);
  Multiplexer multiplexer_1 (.sel(Operand_1), .in_0(A3), .in_1(not_1_out), .out(multiplexer_1_out));
  _7483 _7483_1 (
    .pin1(multiplexer_1_out), .pin2(_7483_1_pin2), .pin3(_7483_1_pin3), .pin4(B2), .pin5(1'b1),
    .pin6(_7483_1_pin6), .pin7(B1), .pin8(_7483_1_pin8), .pin9(_7483_1_pin9), .pin10(_7483_1_pin10),
    .pin11(B0), .pin12(1'b0), .pin13(Operand_1), .pin15(_7483_1_pin15), .pin16(B3));  // open: pin14
  not not_2 (not_2_out, A2);
  Multiplexer multiplexer_2 (.sel(Operand_1), .in_0(A2), .in_1(not_2_out), .out(_7483_1_pin3));
  not not_3 (not_3_out, A1);
  Multiplexer multiplexer_3 (.sel(Operand_1), .in_0(A1), .in_1(not_3_out), .out(_7483_1_pin8));
  not not_4 (not_4_out, A0);
  Multiplexer multiplexer_4 (.sel(Operand_1), .in_0(A0), .in_1(not_4_out), .out(_7483_1_pin10));
  Multiplexer multiplexer_5 (.sel(Operand_2), .in_0(multiplexer_9_out), .in_1(_7483_1_pin15), .out(Y3));
  Multiplexer multiplexer_6 (.sel(Operand_2), .in_0(multiplexer_10_out), .in_1(_7483_1_pin2), .out(Y2));
  Multiplexer multiplexer_7 (.sel(Operand_2), .in_0(multiplexer_11_out), .in_1(_7483_1_pin6), .out(Y1));
  and and_1 (and_1_out, A3, B3);
  Multiplexer multiplexer_8 (.sel(Operand_2), .in_0(multiplexer_12_out), .in_1(_7483_1_pin9), .out(Y0));
  and and_2 (and_2_out, A2, B2);
  and and_3 (and_3_out, A1, B1);
  and and_4 (and_4_out, A0, B0);
  Multiplexer multiplexer_9 (.sel(Operand_1), .in_0(xor_1_out), .in_1(and_1_out), .out(multiplexer_9_out));
  Multiplexer multiplexer_10 (.sel(Operand_1), .in_0(xor_2_out), .in_1(and_2_out), .out(multiplexer_10_out));
  Multiplexer multiplexer_11 (.sel(Operand_1), .in_0(xor_3_out), .in_1(and_3_out), .out(multiplexer_11_out));
  xor xor_1 (xor_1_out, A3, B3);
  Multiplexer multiplexer_12 (.sel(Operand_1), .in_0(xor_4_out), .in_1(and_4_out), .out(multiplexer_12_out));
  xor xor_2 (xor_2_out, A2, B2);
  xor xor_3 (xor_3_out, A1, B1);
  xor xor_4 (xor_4_out, A0, B0);
endmodule
