// Digital circuit 4-bit_ALU_1.dig as structural Verilog
module _4_bit_ALU_1 (
  input  A3,
  input  A2,
  input  A1,
  input  A0,
  input  B3,
  input  B2,
  input  B1,
  input  B0,
  input  C,
  output Y4,
  output Y3,
  output Y1,
  output Y0
);

  wire Full_Adder_1_c_o, Full_Adder_2_c_o, Full_Adder_3_c_o, multiplexer_1_out, multiplexer_2_out,
       multiplexer_3_out, multiplexer_4_out, not_1_out, not_2_out, not_3_out, not_4_out;

  Add Full_Adder_4 (.a(multiplexer_1_out), .b(B3), .c_i(Full_Adder_3_c_o), .s(Y4));  // open: c_o
  Add Full_Adder_3 (.a(multiplexer_2_out), .b(B2), .c_i(Full_Adder_2_c_o), .s(Y3), .c_o(Full_Adder_3_c_o));
  Add Full_Adder_2 (.a(multiplexer_3_out), .b(B1), .c_i(Full_Adder_1_c_o), .s(Y1), .c_o(Full_Adder_2_c_o));
  Add Full_Adder_1 (.a(multiplexer_4_out), .b(B0), .c_i(C), .s(Y0), .c_o(Full_Adder_1_c_o));
  Multiplexer multiplexer_1 (.sel(C), .in_0(A3), .in_1(not_1_out), .out(multiplexer_1_out));
  Multiplexer multiplexer_2 (.sel(C), .in_0(A2), .in_1(not_2_out), .out(multiplexer_2_out));
  not not_1 (not_1_out, A3);
  Multiplexer multiplexer_3 (.sel(C), .in_0(A1), .in_1(not_3_out), .out(multiplexer_3_out));
  not not_2 (not_2_out, A2);
  Multiplexer multiplexer_4 (.sel(C), .in_0(A0), .in_1(not_4_out), .out(multiplexer_4_out));
  not not_3 (not_3_out, A1);
  not not_4 (not_4_out, A0);
endmodule
