// Digital circuit 4-bit_ALU_2.dig as structural Verilog
module _4_bit_ALU_2 (
  input  A0,
  input  A1,
  input  A2,
  input  A3,
  input  B0,
  input  B1,
  input  B2,
  input  B3,
  input  C,
  output Y3,
  output Y2,
  output Y1,
  output Y0
);

  wire _7483_1_pin1, _7483_1_pin3, _7483_1_pin8, _7483_1_pin10, not_1_out, not_2_out, not_3_out, not_4_out;

  _7483 _7483_1 (
    .pin1(_7483_1_pin1), .pin2(Y2), .pin3(_7483_1_pin3), .pin4(B2), .pin5(1'b1), .pin6(Y1), .pin7(B1),
    .pin8(_7483_1_pin8), .pin9(Y0), .pin10(_7483_1_pin10), .pin11(B0), .pin12(1'b0), .pin13(C), .pin15(Y3),
    .pin16(B3));  // open: pin14
  not not_1 (not_1_out, A3);
  not not_2 (not_2_out, A2);
  Multiplexer multiplexer_1 (.sel(C), .in_0(A3), .in_1(not_1_out), .out(_7483_1_pin1));
  not not_3 (not_3_out, A1);
  Multiplexer multiplexer_2 (.sel(C), .in_0(A2), .in_1(not_2_out), .out(_7483_1_pin3));
  not not_4 (not_4_out, A0);
  Multiplexer multiplexer_3 (.sel(C), .in_0(A1), .in_1(not_3_out), .out(_7483_1_pin8));
  Multiplexer multiplexer_4 (.sel(C), .in_0(A0), .in_1(not_4_out), .out(_7483_1_pin10));
endmodule
