// Digital circuit 4-bit_ALU_8.dig as structural Verilog
module _4_bit_ALU_8 (
  input  A0,
  input  A1,
  input  A2,
  input  A3,
  input  B0,
  input  B1,
  input  B2,
  input  B3,
  input  Opcode_1,
  input  Opcode_2,
  output Y7,
  output Y6,
  output Y5,
  output Y4
);

  wire _7483_1_pin1, _7483_1_pin2, _7483_1_pin3, _7483_1_pin6, _7483_1_pin8, _7483_1_pin9, _7483_1_pin10,
       _7483_1_pin15, and_1_out, and_2_out, and_3_out, and_4_out, and_5_out, and_6_out, and_7_out, and_8_out,
       and_9_out, and_10_out, and_11_out, and_12_out, multiplexer_9_out, multiplexer_10_out,
       multiplexer_11_out, multiplexer_12_out, not_1_out, not_2_out, not_3_out, not_4_out, not_5_out,
       not_6_out, not_7_out, not_8_out, or_1_out, or_2_out, or_3_out, or_4_out;

  _7483 _7483_1 (
    .pin1(_7483_1_pin1), .pin2(_7483_1_pin2), .pin3(_7483_1_pin3), .pin4(B2), .pin5(1'b1),
    .pin6(_7483_1_pin6), .pin7(B1), .pin8(_7483_1_pin8), .pin9(_7483_1_pin9), .pin10(_7483_1_pin10),
    .pin11(B0), .pin12(1'b0), .pin13(Opcode_1), .pin15(_7483_1_pin15), .pin16(B3));  // open: pin14
  not not_1 (not_1_out, A3);
  not not_2 (not_2_out, A2);
  Multiplexer multiplexer_1 (.sel(Opcode_1), .in_0(A3), .in_1(not_1_out), .out(_7483_1_pin1));
  not not_3 (not_3_out, A1);
  Multiplexer multiplexer_2 (.sel(Opcode_1), .in_0(A2), .in_1(not_2_out), .out(_7483_1_pin3));
  not not_4 (not_4_out, A0);
  Multiplexer multiplexer_3 (.sel(Opcode_1), .in_0(A1), .in_1(not_3_out), .out(_7483_1_pin8));
  Multiplexer multiplexer_4 (.sel(Opcode_1), .in_0(A0), .in_1(not_4_out), .out(_7483_1_pin10));
  Multiplexer multiplexer_5 (.sel(Opcode_2), .in_0(multiplexer_9_out), .in_1(_7483_1_pin15), .out(Y7));
  not not_5 (not_5_out, Opcode_1);
  Multiplexer multiplexer_6 (.sel(Opcode_2), .in_0(multiplexer_10_out), .in_1(_7483_1_pin2), .out(Y6));
  and and_1 (and_1_out, A3, not_5_out);
  or or_1 (or_1_out, and_2_out, and_1_out);
  Multiplexer multiplexer_7 (.sel(Opcode_2), .in_0(multiplexer_11_out), .in_1(_7483_1_pin6), .out(Y5));
  and and_2 (and_2_out, A2, Opcode_1);
  Multiplexer multiplexer_8 (.sel(Opcode_2), .in_0(multiplexer_12_out), .in_1(_7483_1_pin9), .out(Y4));
  not not_6 (not_6_out, Opcode_1);
  and and_3 (and_3_out, A2, not_6_out);
  or or_2 (or_2_out, and_4_out, and_3_out);
  and and_4 (and_4_out, A1, Opcode_1);
  not not_7 (not_7_out, Opcode_1);
  and and_5 (and_5_out, A1, not_7_out);
  and and_6 (and_6_out, A0, Opcode_1);
  or or_3 (or_3_out, and_6_out, and_5_out);
  Multiplexer multiplexer_9 (.sel(Opcode_1), .in_0(and_9_out), .in_1(or_1_out), .out(multiplexer_9_out));
  not not_8 (not_8_out, Opcode_1);
  Multiplexer multiplexer_10 (.sel(Opcode_1), .in_0(and_10_out), .in_1(or_2_out), .out(multiplexer_10_out));
  and and_7 (and_7_out, A0, not_8_out);
  Multiplexer multiplexer_11 (.sel(Opcode_1), .in_0(and_11_out), .in_1(or_3_out), .out(multiplexer_11_out));
  and and_8 (and_8_out, 1'b0, Opcode_1);
  or or_4 (or_4_out, and_8_out, and_7_out);
  Multiplexer multiplexer_12 (.sel(Opcode_1), .in_0(and_12_out), .in_1(or_4_out), .out(multiplexer_12_out));
  and and_9 (and_9_out, A3, B3);
  and and_10 (and_10_out, A2, B2);
  and and_11 (and_11_out, A1, B1);
  and and_12 (and_12_out, A0, B0);
endmodule
