// Digital circuit Bitwise_AND.dig as structural Verilog
module Bitwise_AND (
  input  A3,
  input  A2,
  input  A1,
  input  A0,
  input  B3,
  input  B2,
  input  B1,
  input  B0,
  output Y0,
  output Y1,
  output Y2,
  output Y3
);

  and and_1 (Y3, B3, A3);
  and and_2 (Y2, B2, A2);
  and and_3 (Y1, B1, A1);
  and and_4 (Y0, B0, A0);
endmodule
