// Digital circuit Shift_left.dig as structural Verilog
module Shift_left (
  input  A3,
  input  A2,
  input  A1,
  input  A0,
  input  Shift_Left,
  output Y3,
  output Y2,
  output Y1,
  output Y0
);

  wire and_1_out, and_2_out, and_3_out, and_4_out, and_5_out, and_6_out, and_7_out, and_8_out, not_1_out,
       not_2_out, not_3_out, not_4_out;

  not not_1 (not_1_out, Shift_Left);
  and and_1 (and_1_out, A3, not_1_out);
  or or_1 (Y3, and_2_out, and_1_out);
  and and_2 (and_2_out, A2, Shift_Left);
  not not_2 (not_2_out, Shift_Left);
  and and_3 (and_3_out, A2, not_2_out);
  and and_4 (and_4_out, A1, Shift_Left);
  or or_2 (Y2, and_4_out, and_3_out);
  not not_3 (not_3_out, Shift_Left);
  and and_5 (and_5_out, A1, not_3_out);
  and and_6 (and_6_out, A0, Shift_Left);
  or or_3 (Y1, and_6_out, and_5_out);
  not not_4 (not_4_out, Shift_Left);
  and and_7 (and_7_out, A0, not_4_out);
  or or_4 (Y0, and_8_out, and_7_out);
  and and_8 (and_8_out, 1'b0, Shift_Left);
endmodule
