// Digital circuit Shift_left_simple.dig as structural Verilog
module Shift_left_simple (
  input  A0,
  input  Shift_Left,
  output Y0
);

  wire and_1_out, and_2_out, not_1_out;

  not not_1 (not_1_out, Shift_Left);
  and and_1 (and_1_out, A0, not_1_out);
  and and_2 (and_2_out, 1'b0, Shift_Left);
  or or_1 (Y0, and_2_out, and_1_out);
endmodule
